# Fritzing sketch ADS8688a_breakboard_v0 (saved by Fritzing 0.9.2b)
circuit board: 4.10593cm x 2.03059cm
breadboards: 1

parts:
  ADC1 = ADS8688a [chip_label=ASD8688A package=TSSOP38]
  J2 = female pin header, 16 pins [form="♀ (female)"]
  X7R = Ceramic Capacitor [capacitance=1µF voltage=10V package="0603 [SMD, multilayer]"]
  X7R_2 = Ceramic Capacitor [capacitance=1µF voltage=10V package="0603 [SMD, multilayer]"]
  X7R_3 = Ceramic Capacitor [capacitance=10µF voltage=10V package="0805 [SMD, multilayer]"]
  X7R_4 = Ceramic Capacitor [capacitance=1µF voltage=10V package="0603 [SMD, multilayer]"]
  22uF_10v = Capacitor [package=1210]
  X7R_5 = Ceramic Capacitor [capacitance=10µF voltage=10V package="0805 [SMD, multilayer]"]
  J3 = female pin header, 9 pins [form="♀ (female)"]

nets:
  N1: ADC1.SDI, J3.pin3
  N2: ADC1.RST/PD, J3.pin4
  N3: ADC1.DAISY, J3.pin5
  N4: ADC1.REFSEL, J3.pin2
  N5: ADC1.REFIO, X7R_5.1
  GND: ADC1.REFGND, ADC1.AGND#28, ADC1.AGND#29, ADC1.AGND#31, ADC1.AGND#32, ADC1.DGND, X7R_2.0, X7R_3.0, X7R_4.1, 22uF_10v.1, X7R_5.0, J3.pin1
  N6: ADC1.REFCAP, X7R_4.0, 22uF_10v.2
  N7: ADC1.AGND#8, X7R.1
  N8: ADC1.AVDD#9, X7R.0
  N9: ADC1.A6IN, J2.pin15
  N10: ADC1.A6GND, J2.pin16
  N11: ADC1.A7IN, J2.pin13
  N12: ADC1.A7GND, J2.pin14
  N13: ADC1.A0IN, J2.pin1
  N14: ADC1.A0GND, J2.pin2
  N15: ADC1.A1IN, J2.pin3
  N16: ADC1.A1GND, J2.pin4
  N17: ADC1.A2GND, J2.pin6
  N18: ADC1.A2IN, J2.pin5
  N19: ADC1.A3GND, J2.pin8
  N20: ADC1.A3IN, J2.pin7
  N21: ADC1.A4GND, J2.pin10
  N22: ADC1.A4IN, J2.pin9
  N23: ADC1.A5GND, J2.pin12
  N24: ADC1.A5IN, J2.pin11
  5V: ADC1.AVDD#30, ADC1.DVDD, X7R_2.1, X7R_3.1, J3.pin9
  N25: ADC1.SDO, J3.pin8
  N26: ADC1.SCLK, J3.pin7
  N27: ADC1.CS, J3.pin6
