# Fritzing sketch ADS8688a_breakboard_v1 (saved by Fritzing 0.9.2b)
circuit board: 4.5985cm x 2.3053cm

parts:
  ADC1 = ADS8688a [chip_label=ASD8688A package=TSSOP38]
  X7R = Ceramic Capacitor [capacitance=1µF voltage=10V package="0603 [SMD, multilayer]"]
  X7R_2 = Ceramic Capacitor [capacitance=1µF voltage=10V package="0603 [SMD, multilayer]"]
  X7R_3 = Ceramic Capacitor [capacitance=10µF voltage=10V package="0805 [SMD, multilayer]"]
  X7R_4 = Ceramic Capacitor [capacitance=1µF voltage=10V package="0603 [SMD, multilayer]"]
  22uF_10v = Capacitor [package=1210]
  X7R_5 = Ceramic Capacitor [capacitance=10µF voltage=10V package="0805 [SMD, multilayer]"]
  J2 = female pin header, 18 pins [form="♀ (female)"]
  J4 = female pin header, 12 pins [form="♀ (female)"]

nets:
  SDI: ADC1.SDI, J4.pin4
  RST: ADC1.RST/PD, J4.pin5
  DAISY: ADC1.DAISY, J4.pin6
  REFSEL: ADC1.REFSEL, J4.pin3
  REFIO: ADC1.REFIO, X7R_5.1, J4.pin2
  GND: ADC1.REFGND, ADC1.AGND, ADC1.DGND, X7R.1, X7R_2.0, X7R_3.0, X7R_4.1, 22uF_10v.1, X7R_5.0, J4.pin1
  N1: ADC1.REFCAP, X7R_4.0, 22uF_10v.2
  AVDD: ADC1.AVDD, X7R.0, X7R_2.1, J4.pin12
  AUXIN: ADC1.AUXIN, J2.pin17
  AUXGND: ADC1.AUXGND, J2.pin18
  A6IN: ADC1.A6IN, J2.pin13
  A6GND: ADC1.A6GND, J2.pin14
  A7IN: ADC1.A7IN, J2.pin15
  A7GND: ADC1.A7GND, J2.pin16
  A0IN: ADC1.A0IN, J2.pin1
  A0GND: ADC1.A0GND, J2.pin2
  A1IN: ADC1.A1IN, J2.pin3
  A1GND: ADC1.A1GND, J2.pin4
  A2GND: ADC1.A2GND, J2.pin6
  A2IN: ADC1.A2IN, J2.pin5
  A3GND: ADC1.A3GND, J2.pin8
  A3IN: ADC1.A3IN, J2.pin7
  A4GND: ADC1.A4GND, J2.pin10
  A4IN: ADC1.A4IN, J2.pin9
  A5GND: ADC1.A5GND, J2.pin12
  A5IN: ADC1.A5IN, J2.pin11
  DVDD: ADC1.DVDD, X7R_3.1, J4.pin11
  ALARM: ADC1.ALARM, J4.pin10
  SDO: ADC1.SDO, J4.pin9
  SCLK: ADC1.SCLK, J4.pin8
  CS: ADC1.CS, J4.pin7

notes:
  ADS8688a
  breakboard v1.0
  A0IN
  GND
  REFIO
  REFSEL
  SDI
  RST/PD
  DAISY
  CS
  SCLK
  SDO
  ALARM
  DVDD
  AVDD
  A0GND
  A1IN
  A1GND
  A2IN
  A2GND
  A3IN
  A3GND
  A4IN
  A4GND
  A5IN
  A5GND
  A6IN
  A6GND
  A7IN
  A7GND
  AUXIN
  AUXOUT
  internal connection 8-31... et ce serait tout...
